// Logisim project Computer.circ as structural Verilog
module instruction_fetch (
  input  [31:0] in_1
);

  wire PC_SRC;
  wire [31:0] adder_1_out, instruction_memory_subsystem_1_read_data, multiplexer_1_out, PROGRAM_COUNTER_q;

  Multiplexer #(.width(32)) multiplexer_1 (.in1(adder_1_out), .out(multiplexer_1_out), .sel(PC_SRC));  // open: in0
  Register #(.width(32)) PROGRAM_COUNTER (.D(multiplexer_1_out), .Q(PROGRAM_COUNTER_q));  // open: en, clk, clr
  Adder #(.width(32)) adder_1 (.a(PROGRAM_COUNTER_q), .b(in_1), .out(adder_1_out));  // open: cin, cout
  instruction_memory_subsystem instruction_memory_subsystem_1 (
    .ADDRESS(PROGRAM_COUNTER_q), .READ_DATA(instruction_memory_subsystem_1_read_data));
  if_id_register if_id_register_1 (
    .PC_in(PROGRAM_COUNTER_q), .inst_in(instruction_memory_subsystem_1_read_data));  // open: CLK, stall, flush, reset, valid_bit_in, PC_out, inst_out, valid_bit_out

  // Notes on the sheet:
  //   in_1: initial=0x4
endmodule

module instruction_memory_subsystem (
  input  [31:0] ADDRESS,
  output [31:0] READ_DATA
);

  wire Bit, comparator_1_lt;
  wire [15:0] multiplexer_1_out;
  wire [31:0] RD1, RD2;

  Multiplexer #(.width(16)) multiplexer_1 (
    .in0(ADDRESS[15:0]), .in1(ADDRESS[31:16]), .out(multiplexer_1_out), .sel(Bit));
  Comparator #(.width(32)) comparator_1 (.a(ADDRESS), .b(32'h10000), .lt(comparator_1_lt));  // open: gt, eq
  not not_1 (Bit, comparator_1_lt);
  ROM #(.addrWidth(16), .dataWidth(32)) rom_1 (.addr(multiplexer_1_out), .data(RD1));
  ROM #(.addrWidth(16), .dataWidth(32)) rom_2 (.addr(multiplexer_1_out), .data(RD2));
  Multiplexer #(.width(32)) multiplexer_2 (.in0(RD1), .in1(RD2), .out(READ_DATA), .sel(Bit));
endmodule

module if_id_register (
  input  CLK,
  input  [31:0] PC_in,
  input  stall,
  input  [31:0] inst_in,
  input  flush,
  input  reset,
  input  valid_bit_in,
  output [31:0] PC_out,
  output [31:0] inst_out,
  output valid_bit_out
);

  wire not_1_out, not_2_out, not_3_out;

  not not_1 (not_1_out, stall);
  not not_2 (not_2_out, stall);
  not not_3 (not_3_out, stall);
  Register #(.width(32)) PC_reg (.D(PC_in), .en(not_1_out), .clk(CLK), .Q(PC_out), .clr(reset));
  Register #(.width(32)) IF_reg (.D(inst_in), .en(not_2_out), .clk(CLK), .Q(inst_out), .clr(reset));
  Register #(.width(1)) register_1 (.D(valid_bit_in), .en(not_3_out), .clk(CLK), .Q(valid_bit_out), .clr(reset));
endmodule

module instruction_splitter (
  input  [31:0] instruction,
  output [6:0] opcode,
  output [4:0] rd,
  output [2:0] funct3,
  output [4:0] rs1,
  output [4:0] rs2,
  output [6:0] funct7
);


  assign funct3 = instruction[14:12];
  assign funct7 = instruction[31:25];
  assign opcode = instruction[6:0];
  assign rd = instruction[11:7];
  assign rs1 = instruction[19:15];
  assign rs2 = instruction[24:20];

  // Notes on the sheet:
  //   opcode
  //   funct3
  //   funct7
  //   rd
  //   rs1
  //   rs2
endmodule

module instruction_decode (
  input  [31:0] in_1
);

  wire [4:0] instruction_splitter_1_rs1, instruction_splitter_1_rs2;

  instruction_splitter instruction_splitter_1 (
    .instruction(in_1), .rs1(instruction_splitter_1_rs1), .rs2(instruction_splitter_1_rs2));  // open: opcode, rd, funct3, funct7
  register_file_subsystem register_file_subsystem_1 (
    .ADDRESS_R_1(instruction_splitter_1_rs1), .ADDRESS_R_2(instruction_splitter_1_rs2));  // open: ADDRESS_W_3, CLK, WRITE_ENABLE, WRITE_DATA, READ_DATA_1, READ_DATA_2
endmodule

module register_file_subsystem (
  input  [4:0] ADDRESS_R_1,
  input  [4:0] ADDRESS_R_2,
  input  [4:0] ADDRESS_W_3,
  input  CLK,
  input  WRITE_ENABLE,
  input  [31:0] WRITE_DATA,
  output [31:0] READ_DATA_1,
  output [31:0] READ_DATA_2
);

  wire E0, E1, E2, E3, E4, E5, E6, E7, E8, E9, E10, E11, E12, E13, E14, E15, E16, E17, E18, E19, E20, E21,
       E22, E23, E24, E25, E26, E27, E28, E29, E30, E31, E32;
  wire [4:0] ADDRESS_W_3_t;
  wire [31:0] Q0, Q1, Q2, Q3, Q4, Q5, Q6, Q7, Q8, Q9, Q10, Q11, Q12, Q13, Q14, Q15, Q16, Q17, Q18, Q19, Q20,
       Q21, Q22, Q23, Q24, Q25, Q26, Q27, Q28, Q29, Q30, Q31;

  Register #(.width(32)) register_1 (.en(E0), .clk(CLK), .Q(Q0), .clr(1'b1));  // open: D
  Register #(.width(32)) register_2 (.D(WRITE_DATA), .en(E1), .clk(CLK), .Q(Q1));  // open: clr
  Register #(.width(32)) register_3 (.D(WRITE_DATA), .en(E2), .clk(CLK), .Q(Q2));  // open: clr
  Register #(.width(32)) register_4 (.D(WRITE_DATA), .en(E3), .clk(CLK), .Q(Q3));  // open: clr
  Decoder #(.select(5)) decoder_1 (
    .out0(E0), .out1(E1), .out2(E2), .out3(E3), .out4(E4), .out5(E5), .out6(E6), .out7(E7), .out8(E8),
    .out9(E9), .out10(E10), .out11(E11), .out12(E12), .out13(E13), .out14(E14), .out15(E15), .out16(E16),
    .out17(E17), .out18(E18), .out19(E19), .out20(E20), .out21(E21), .out22(E22), .out23(E23), .out24(E24),
    .out25(E25), .out26(E26), .out27(E27), .out28(E28), .out29(E29), .out30(E30), .out31(E31),
    .sel(ADDRESS_W_3_t), .en(WRITE_ENABLE));
  Register #(.width(32)) register_5 (.D(WRITE_DATA), .en(E5), .clk(CLK), .Q(Q4));  // open: clr
  Register #(.width(32)) register_6 (.D(WRITE_DATA), .en(E6), .clk(CLK), .Q(Q5));  // open: clr
  Register #(.width(32)) register_7 (.D(WRITE_DATA), .en(E7), .clk(CLK), .Q(Q6));  // open: clr
  Register #(.width(32)) register_8 (.D(WRITE_DATA), .en(E8), .clk(CLK), .Q(Q7));  // open: clr
  Multiplexer #(.select(5), .width(32)) multiplexer_1 (
    .in0(Q0), .in1(Q1), .in2(Q2), .in3(Q3), .in4(Q4), .in5(Q5), .in6(Q6), .in7(Q7), .in8(Q8), .in9(Q9),
    .in10(Q10), .in11(Q11), .in12(Q12), .in13(Q13), .in14(Q14), .in15(Q15), .in16(Q16), .in17(Q17),
    .in18(Q18), .in19(Q19), .in20(Q20), .in21(Q21), .in22(Q22), .in23(Q23), .in24(Q24), .in25(Q25),
    .in26(Q26), .in27(Q27), .in28(Q28), .in29(Q29), .in30(Q30), .in31(Q31), .out(READ_DATA_1),
    .sel(ADDRESS_R_1));
  Register #(.width(32)) register_9 (.D(WRITE_DATA), .en(E9), .clk(CLK), .Q(Q8));  // open: clr
  Register #(.width(32)) register_10 (.D(WRITE_DATA), .en(E10), .clk(CLK), .Q(Q9));  // open: clr
  Register #(.width(32)) register_11 (.D(WRITE_DATA), .en(E11), .clk(CLK), .Q(Q10));  // open: clr
  Register #(.width(32)) register_12 (.D(WRITE_DATA), .en(E12), .clk(CLK), .Q(Q11));  // open: clr
  Register #(.width(32)) register_13 (.D(WRITE_DATA), .en(E13), .clk(CLK), .Q(Q12));  // open: clr
  Register #(.width(32)) register_14 (.D(WRITE_DATA), .en(E14), .clk(CLK), .Q(Q13));  // open: clr
  Register #(.width(32)) register_15 (.D(WRITE_DATA), .en(E15), .clk(CLK), .Q(Q14));  // open: clr
  Register #(.width(32)) register_16 (.D(WRITE_DATA), .en(E16), .clk(CLK), .Q(Q15));  // open: clr
  Register #(.width(32)) register_17 (.D(WRITE_DATA), .en(E17), .clk(CLK), .Q(Q16));  // open: clr
  Register #(.width(32)) register_18 (.D(WRITE_DATA), .en(E18), .clk(CLK), .Q(Q17));  // open: clr
  Register #(.width(32)) register_19 (.D(WRITE_DATA), .en(E19), .clk(CLK), .Q(Q18));  // open: clr
  Register #(.width(32)) register_20 (.D(WRITE_DATA), .en(E20), .clk(CLK), .Q(Q19));  // open: clr
  Register #(.width(32)) register_21 (.D(WRITE_DATA), .en(E21), .clk(CLK), .Q(Q20));  // open: clr
  Register #(.width(32)) register_22 (.D(WRITE_DATA), .en(E22), .clk(CLK), .Q(Q21));  // open: clr
  Register #(.width(32)) register_23 (.D(WRITE_DATA), .en(E23), .clk(CLK), .Q(Q22));  // open: clr
  Register #(.width(32)) register_24 (.D(WRITE_DATA), .en(E24), .clk(CLK), .Q(Q23));  // open: clr
  Multiplexer #(.select(5), .width(32)) multiplexer_2 (
    .in0(Q0), .in1(Q1), .in2(Q2), .in3(Q3), .in4(Q4), .in5(Q5), .in6(Q6), .in7(Q7), .in8(Q8), .in9(Q9),
    .in10(Q10), .in11(Q11), .in12(Q12), .in13(Q13), .in14(Q14), .in15(Q15), .in16(Q16), .in17(Q17),
    .in18(Q18), .in19(Q19), .in20(Q20), .in21(Q21), .in22(Q22), .in23(Q23), .in24(Q24), .in25(Q25),
    .in26(Q26), .in27(Q27), .in28(Q28), .in29(Q29), .in30(Q30), .in31(Q31), .out(READ_DATA_2),
    .sel(ADDRESS_R_2));
  Register #(.width(32)) register_25 (.D(WRITE_DATA), .en(E25), .clk(CLK), .Q(Q24));  // open: clr
  Register #(.width(32)) register_26 (.D(WRITE_DATA), .en(E26), .clk(CLK), .Q(Q25));  // open: clr
  Register #(.width(32)) register_27 (.D(WRITE_DATA), .en(E27), .clk(CLK), .Q(Q26));  // open: clr
  Register #(.width(32)) register_28 (.D(WRITE_DATA), .en(E28), .clk(CLK), .Q(Q27));  // open: clr
  Register #(.width(32)) register_29 (.D(WRITE_DATA), .en(E29), .clk(CLK), .Q(Q28));  // open: clr
  Register #(.width(32)) register_30 (.D(WRITE_DATA), .en(E30), .clk(CLK), .Q(Q29));  // open: clr
  Register #(.width(32)) register_31 (.D(WRITE_DATA), .en(E31), .clk(CLK), .Q(Q30));  // open: clr
  Register #(.width(32)) register_32 (.D(WRITE_DATA), .en(E32), .clk(CLK), .Q(Q31));  // open: clr

  // Other names for the same wires on the sheet: ADDRESS_1[4:0] = ADDRESS_R_1; ADDRESS_2[4:0] = ADDRESS_R_2;
  //   ADDRESS_3[4:0] = ADDRESS_W_3; WD[31:0] = WRITE_DATA; WE3 = WRITE_ENABLE
endmodule

module data_memory_subsystem (
  input  [31:0] ADDRESS,
  input  [31:0] WRITE_DATA,
  input  WRITE_ENABLE,
  input  CLK,
  output [31:0] READ_DATA
);

  wire Bit, comparator_1_lt;
  wire [15:0] multiplexer_1_out;
  wire [31:0] RD1, RD2;

  Multiplexer #(.width(16)) multiplexer_1 (
    .in0(ADDRESS[15:0]), .in1(ADDRESS[31:16]), .out(multiplexer_1_out), .sel(Bit));
  Comparator #(.width(32)) comparator_1 (.a(ADDRESS), .b(32'h10000), .lt(comparator_1_lt));  // open: gt, eq
  not not_1 (Bit, comparator_1_lt);
  RAM #(.addrWidth(16), .dataWidth(32)) ram_1 (
    .addr(multiplexer_1_out), .we(WRITE_ENABLE), .oe(1'b1), .clk(CLK), .din(WRITE_DATA), .dout(RD1));
  RAM #(.addrWidth(16), .dataWidth(32)) ram_2 (
    .addr(multiplexer_1_out), .we(WRITE_ENABLE), .oe(1'b1), .clk(CLK), .din(WRITE_DATA), .dout(RD2));
  Multiplexer #(.width(32)) multiplexer_2 (.in0(RD1), .in1(RD2), .out(READ_DATA), .sel(Bit));
endmodule

module immediate_generator (
  input  [31:0] INSTRUCTION_IN,
  output [31:0] IMMEDIATE_OUT
);


  // Other names for the same wires on the sheet: INSTRUCTION[31:0] = INSTRUCTION_IN
endmodule
